// Logisim project 16bitadder.circ as structural Verilog: 2 circuits, main circuit main
module main (
  input  [15:0] B,
  input  sub,
  input  [15:0] A,
  output ovf,
  output [15:0] result
);

  wire temp_1_out_5, temp_2_out_5, temp_3_out_5, temp_4_out_5, temp_5_out_5, temp_6_out_5, temp_7_out_5,
       temp_8_out_5, temp_9_out_5, temp_10_out_5, temp_11_out_5, temp_12_out_5, temp_13_out_5, temp_14_out_5,
       temp_15_out_5, temp_16_out_5, xor_1_out, xor_2_out, xor_3_out, xor_4_out, xor_5_out, xor_6_out,
       xor_7_out, xor_8_out, xor_9_out, xor_10_out, xor_11_out, xor_12_out, xor_13_out, xor_14_out,
       xor_15_out, xor_16_out;

  xor xor_1 (xor_1_out, B[0], sub);
  temp temp_1 (.in_1(sub), .in_2(A[0]), .in_3(xor_1_out), .out_4(result[0]), .out_5(temp_1_out_5));
  xor xor_2 (xor_2_out, B[1], sub);
  temp temp_2 (.in_1(temp_1_out_5), .in_2(A[1]), .in_3(xor_2_out), .out_4(result[1]), .out_5(temp_2_out_5));
  xor xor_3 (xor_3_out, B[2], sub);
  temp temp_3 (.in_1(temp_2_out_5), .in_2(A[2]), .in_3(xor_3_out), .out_4(result[2]), .out_5(temp_3_out_5));
  xor xor_4 (xor_4_out, B[3], sub);
  temp temp_4 (.in_1(temp_3_out_5), .in_2(A[3]), .in_3(xor_4_out), .out_4(result[3]), .out_5(temp_4_out_5));
  xor xor_5 (xor_5_out, B[4], sub);
  temp temp_5 (.in_1(temp_4_out_5), .in_2(A[4]), .in_3(xor_5_out), .out_4(result[4]), .out_5(temp_5_out_5));
  xor xor_6 (xor_6_out, B[5], sub);
  temp temp_6 (.in_1(temp_5_out_5), .in_2(A[5]), .in_3(xor_6_out), .out_4(result[5]), .out_5(temp_6_out_5));
  xor xor_7 (xor_7_out, B[6], sub);
  temp temp_7 (.in_1(temp_6_out_5), .in_2(A[6]), .in_3(xor_7_out), .out_4(result[6]), .out_5(temp_7_out_5));
  xor xor_8 (xor_8_out, B[7], sub);
  temp temp_8 (.in_1(temp_7_out_5), .in_2(A[7]), .in_3(xor_8_out), .out_4(result[7]), .out_5(temp_8_out_5));
  xor xor_9 (xor_9_out, B[8], sub);
  temp temp_9 (.in_1(temp_8_out_5), .in_2(A[8]), .in_3(xor_9_out), .out_4(result[8]), .out_5(temp_9_out_5));
  xor xor_10 (xor_10_out, B[9], sub);
  temp temp_10 (.in_1(temp_9_out_5), .in_2(A[9]), .in_3(xor_10_out), .out_4(result[9]), .out_5(temp_10_out_5));
  xor xor_11 (xor_11_out, B[10], sub);
  temp temp_11 (.in_1(temp_10_out_5), .in_2(A[10]), .in_3(xor_11_out), .out_4(result[10]), .out_5(temp_11_out_5));
  xor xor_12 (xor_12_out, B[11], sub);
  temp temp_12 (.in_1(temp_11_out_5), .in_2(A[11]), .in_3(xor_12_out), .out_4(result[11]), .out_5(temp_12_out_5));
  xor xor_13 (xor_13_out, B[12], sub);
  temp temp_13 (.in_1(temp_12_out_5), .in_2(A[12]), .in_3(xor_13_out), .out_4(result[12]), .out_5(temp_13_out_5));
  xor xor_14 (xor_14_out, B[13], sub);
  temp temp_14 (.in_1(temp_13_out_5), .in_2(A[13]), .in_3(xor_14_out), .out_4(result[13]), .out_5(temp_14_out_5));
  xor xor_15 (xor_15_out, B[14], sub);
  temp temp_15 (.in_1(temp_14_out_5), .in_2(A[14]), .in_3(xor_15_out), .out_4(result[14]), .out_5(temp_15_out_5));
  xor xor_16 (xor_16_out, B[15], sub);
  temp temp_16 (.in_1(temp_15_out_5), .in_2(A[15]), .in_3(xor_16_out), .out_4(result[15]), .out_5(temp_16_out_5));
  xor xor_17 (ovf, temp_15_out_5, temp_16_out_5);
endmodule

module temp (
  input  in_1,
  input  in_2,
  input  in_3,
  output out_4,
  output out_5
);

  wire and_1_out, and_2_out, xor_1_out;

  xor xor_1 (xor_1_out, in_2, in_3);
  and and_1 (and_1_out, in_1, xor_1_out);
  and and_2 (and_2_out, in_3, in_2);
  xor xor_2 (out_4, xor_1_out, in_1);
  or or_1 (out_5, and_1_out, and_2_out);
endmodule
