// Logisim project CPU.circ as structural Verilog: 19 circuits, main circuit main
module main (
  input  reset
);

  wire alu_beq, alu_bgt, and_1_out, and_2_out, clk, control_aluop, control_beq, control_bgt,
       control_immediate, control_input, control_j, control_jal, control_jr, control_lw, control_output,
       control_rdst, control_sw, control_we, keyboard_1_avail, memorylatch_1_oe_latched,
       memorylatch_1_we_latched, not_1_out, not_2_out, not_3_out, not_4_out;
  wire [2:0] aludecode_1_aludecode_optype, controlled_buffer_1_out, mips_rd, mips_rs, mips_rt, mips_shamt,
       multiplexer_3_out;
  wire [3:0] mips_opcode;
  wire [5:0] mips_immediate;
  wire [6:0] keyboard_1_data;
  wire [7:0] mips_rd_val;
  wire [11:0] mips_address;
  wire [15:0] alu_1_out_4, alu_pcincrement, alubranch_1_alubranch_address, alubranch_2_alubranch_address,
       alujump_1_alujump_jaddress, memorylatch_1_address_latched, memorylatch_1_data_in_latched, mips_rs_val,
       mips_signextend, multiplexer_1_out, multiplexer_2_out, multiplexer_4_out, multiplexer_5_out,
       multiplexer_6_out, multiplexer_7_out, multiplexer_8_out, multiplexer_9_out, pc_1_pc_address_output,
       ram_1_dout, registerfile_1_regfile_rs2_out, rom_1_data;

  Clock u_clk (.out(clk));
  pc pc_1 (
    .pc_address_input(multiplexer_7_out), .pc_clk(clk), .reset(reset),
    .pc_address_output(pc_1_pc_address_output));
  alupcincrement alupcincrement_1 (.alupcincrement_input(pc_1_pc_address_output), .out_2(alu_pcincrement));
  ROM #(.addrWidth(16), .dataWidth(16)) rom_1 (.addr(pc_1_pc_address_output), .data(rom_1_data));
  alubranch alubranch_1 (
    .alubranch_pc(alu_pcincrement), .alubranch_immediate(mips_signextend),
    .alubranch_address(alubranch_1_alubranch_address));
  and and_1 (and_1_out, control_beq, alu_beq);
  Multiplexer #(.width(16), .disabled("Z"), .enable("false")) multiplexer_1 (
    .in0(alu_pcincrement), .in1(alubranch_1_alubranch_address), .out(multiplexer_1_out), .sel(and_1_out));
  not not_1 (not_1_out, alu_beq);
  assign controlled_buffer_1_out = control_jal ? 3'b111 : 3'bz;  // Controlled_Buffer controlled_buffer_1
  assign controlled_buffer_1_out = not_2_out ? mips_rd : 3'bz;  // Controlled_Buffer controlled_buffer_2
  not not_2 (not_2_out, control_jal);
  instructions instructions_1 (
    .instructions_input(rom_1_data), .instructions_shamt(mips_shamt), .instructions_rd(mips_rd),
    .instructions_rt(mips_rt), .instructions_rs(mips_rs), .instructions_opcode(mips_opcode),
    .instructions_immediate(mips_immediate), .instructions_address(mips_address));
  control control_1 (
    .control_optype(mips_opcode), .control_output(control_output), .control_input(control_input),
    .control_lw(control_lw), .control_sw(control_sw), .control_beq(control_beq), .control_bgt(control_bgt),
    .control_aluop(control_aluop), .control_j(control_j), .control_jal(control_jal), .control_jr(control_jr),
    .control_we(control_we), .control_immediate(control_immediate), .control_rdst(control_rdst));
  Multiplexer #(.width(16), .disabled("Z"), .enable("false")) multiplexer_2 (
    .in0(multiplexer_1_out), .in1(alubranch_2_alubranch_address), .out(multiplexer_2_out), .sel(and_2_out));
  alubranch alubranch_2 (
    .alubranch_pc(alu_pcincrement), .alubranch_immediate(mips_signextend),
    .alubranch_address(alubranch_2_alubranch_address));
  and and_2 (and_2_out, control_bgt, not_1_out, alu_bgt);
  Multiplexer #(.width(3), .enable("false")) multiplexer_3 (
    .in0(mips_rt), .in1(controlled_buffer_1_out), .out(multiplexer_3_out), .sel(control_rdst));
  not not_3 (not_3_out, clk);
  Multiplexer #(.width(16), .disabled("Z"), .enable("false")) multiplexer_4 (
    .in0(multiplexer_9_out), .in1({{8{1'b0}}, mips_rd_val}), .out(multiplexer_4_out), .sel(control_input));
  RegisterFile registerfile_1 (
    .regfile_rd(multiplexer_3_out), .regfile_we(control_we), .regfile_datain(multiplexer_4_out),
    .regfile_clk(not_3_out), .reset(reset), .regfile_rs2(mips_rt), .regfile_rs1(mips_rs),
    .regfile_rs1_out(mips_rs_val), .regfile_rs2_out(registerfile_1_regfile_rs2_out));
  alujump alujump_1 (
    .alujump_j(mips_address), .alujump_pc(alu_pcincrement), .alujump_jaddress(alujump_1_alujump_jaddress));
  Multiplexer #(.width(16), .disabled("Z"), .enable("false")) multiplexer_5 (
    .in0(multiplexer_2_out), .in1(alujump_1_alujump_jaddress), .out(multiplexer_5_out), .sel(control_j));
  TTY #(.rows(13), .cols(80), .trigger("falling")) tty_1 (
    .data(mips_rs_val[6:0]), .clk(clk), .we(control_output), .clr(reset));
  signextend signextend_1 (.signextend_immediate(mips_immediate), .signextend_output(mips_signextend));
  Multiplexer #(.width(16), .disabled("Z"), .enable("false")) multiplexer_6 (
    .in0(registerfile_1_regfile_rs2_out), .in1(mips_signextend), .out(multiplexer_6_out),
    .sel(control_immediate));
  Keyboard keyboard_1 (.clk(clk), .re(control_input), .clr(reset), .avail(keyboard_1_avail), .data(keyboard_1_data));
  Multiplexer #(.width(16), .disabled("Z"), .enable("false")) multiplexer_7 (
    .in0(multiplexer_5_out), .in1(mips_rs_val), .out(multiplexer_7_out), .sel(control_jr));
  alu alu_1 (
    .alu_a(mips_rs_val), .alu_b(multiplexer_6_out), .alu_muxselector(aludecode_1_aludecode_optype),
    .out_4(alu_1_out_4), .out_5(alu_bgt), .a_b(alu_beq));
  aludecode aludecode_1 (
    .aludecode_controlop(control_aluop), .aludecode_opcode(mips_opcode),
    .aludecode_optype(aludecode_1_aludecode_optype));
  assign mips_rd_val[6:0] = keyboard_1_avail ? keyboard_1_data : 7'bz;  // Controlled_Buffer controlled_buffer_3
  not not_4 (not_4_out, keyboard_1_avail);
  not not_5 (mips_rd_val[7], keyboard_1_avail);
  assign mips_rd_val[6:0] = not_4_out ? {7{1'b0}} : 7'bz;  // Controlled_Buffer controlled_buffer_4
  RAM #(.addrWidth(16), .dataWidth(16), .trigger("high"), .databus("bibus")) ram_1 (
    .addr(memorylatch_1_address_latched), .we(memorylatch_1_we_latched), .oe(memorylatch_1_oe_latched),
    .din(memorylatch_1_data_in_latched), .dout(ram_1_dout));
  memorylatch memorylatch_1 (
    .address(alu_1_out_4), .WE(control_sw), .clk(clk), .data_in(registerfile_1_regfile_rs2_out),
    .address_latched(memorylatch_1_address_latched), .WE_latched(memorylatch_1_we_latched),
    .OE_latched(memorylatch_1_oe_latched), .data_in_latched(memorylatch_1_data_in_latched));
  Multiplexer #(.width(16), .disabled("Z"), .enable("false")) multiplexer_8 (
    .in0(alu_1_out_4), .in1(ram_1_dout), .out(multiplexer_8_out), .sel(control_lw));
  Multiplexer #(.width(16), .disabled("Z"), .enable("false")) multiplexer_9 (
    .in0(multiplexer_8_out), .in1(alu_pcincrement), .out(multiplexer_9_out), .sel(control_jal));

  // Notes on the sheet:
  //   contents of rom_1 (hex, n*v repeats v):
  //   8100 8903 1008 82a0 400 893f 583b 403f
endmodule

module register (
  input  [15:0] reg_datain,
  input  reg_clk,
  input  reg_we,
  input  reset,
  output [15:0] reg_dataout
);

  wire and_1_out;

  and and_1 (and_1_out, reg_clk, reg_we);
  D_Flip_Flop d_ff_1 (.D(reg_datain[0]), .clk(and_1_out), .Q(reg_dataout[0]), .reset(reset));  // open: Qn, preset
  D_Flip_Flop d_ff_2 (.D(reg_datain[1]), .clk(and_1_out), .Q(reg_dataout[1]), .reset(reset));  // open: Qn, preset
  D_Flip_Flop d_ff_3 (.D(reg_datain[2]), .clk(and_1_out), .Q(reg_dataout[2]), .reset(reset));  // open: Qn, preset
  D_Flip_Flop d_ff_4 (.D(reg_datain[3]), .clk(and_1_out), .Q(reg_dataout[3]), .reset(reset));  // open: Qn, preset
  D_Flip_Flop d_ff_5 (.D(reg_datain[4]), .clk(and_1_out), .Q(reg_dataout[4]), .reset(reset));  // open: Qn, preset
  D_Flip_Flop d_ff_6 (.D(reg_datain[5]), .clk(and_1_out), .Q(reg_dataout[5]), .reset(reset));  // open: Qn, preset
  D_Flip_Flop d_ff_7 (.D(reg_datain[6]), .clk(and_1_out), .Q(reg_dataout[6]), .reset(reset));  // open: Qn, preset
  D_Flip_Flop d_ff_8 (.D(reg_datain[7]), .clk(and_1_out), .Q(reg_dataout[7]), .reset(reset));  // open: Qn, preset
  D_Flip_Flop d_ff_9 (.D(reg_datain[8]), .clk(and_1_out), .Q(reg_dataout[8]), .reset(reset));  // open: Qn, preset
  D_Flip_Flop d_ff_10 (.D(reg_datain[9]), .clk(and_1_out), .Q(reg_dataout[9]), .reset(reset));  // open: Qn, preset
  D_Flip_Flop d_ff_11 (.D(reg_datain[10]), .clk(and_1_out), .Q(reg_dataout[10]), .reset(reset));  // open: Qn, preset
  D_Flip_Flop d_ff_12 (.D(reg_datain[11]), .clk(and_1_out), .Q(reg_dataout[11]), .reset(reset));  // open: Qn, preset
  D_Flip_Flop d_ff_13 (.D(reg_datain[12]), .clk(and_1_out), .Q(reg_dataout[12]), .reset(reset));  // open: Qn, preset
  D_Flip_Flop d_ff_14 (.D(reg_datain[13]), .clk(and_1_out), .Q(reg_dataout[13]), .reset(reset));  // open: Qn, preset
  D_Flip_Flop d_ff_15 (.D(reg_datain[14]), .clk(and_1_out), .Q(reg_dataout[14]), .reset(reset));  // open: Qn, preset
  D_Flip_Flop d_ff_16 (.D(reg_datain[15]), .clk(and_1_out), .Q(reg_dataout[15]), .reset(reset));  // open: Qn, preset

  // Other names for the same wires on the sheet: reset_tun = reset
endmodule

module RegisterFile (
  input  [2:0] regfile_rd,
  input  regfile_we,
  input  [15:0] regfile_datain,
  input  regfile_clk,
  input  reset,
  input  [2:0] regfile_rs2,
  input  [2:0] regfile_rs1,
  output [15:0] regfile_rs1_out,
  output [15:0] regfile_rs2_out
);

  wire decoder_1_out1, decoder_1_out2, decoder_1_out3, decoder_1_out4, decoder_1_out5, decoder_1_out6,
       decoder_1_out7;
  wire [15:0] register_1_reg_dataout, register_2_reg_dataout, register_3_reg_dataout, register_4_reg_dataout,
       register_5_reg_dataout, register_6_reg_dataout, register_7_reg_dataout;

  Decoder #(.select(3)) decoder_1 (
    .out1(decoder_1_out1), .out2(decoder_1_out2), .out3(decoder_1_out3), .out4(decoder_1_out4),
    .out5(decoder_1_out5), .out6(decoder_1_out6), .out7(decoder_1_out7), .sel(regfile_rd), .en(regfile_we));  // open: out0
  register register_1 (
    .reg_datain(regfile_datain), .reg_clk(regfile_clk), .reg_we(decoder_1_out1), .reset(reset),
    .reg_dataout(register_1_reg_dataout));
  register register_2 (
    .reg_datain(regfile_datain), .reg_clk(regfile_clk), .reg_we(decoder_1_out2), .reset(reset),
    .reg_dataout(register_2_reg_dataout));
  register register_3 (
    .reg_datain(regfile_datain), .reg_clk(regfile_clk), .reg_we(decoder_1_out3), .reset(reset),
    .reg_dataout(register_3_reg_dataout));
  register register_4 (
    .reg_datain(regfile_datain), .reg_clk(regfile_clk), .reg_we(decoder_1_out4), .reset(reset),
    .reg_dataout(register_4_reg_dataout));
  register register_5 (
    .reg_datain(regfile_datain), .reg_clk(regfile_clk), .reg_we(decoder_1_out5), .reset(reset),
    .reg_dataout(register_5_reg_dataout));
  register register_6 (
    .reg_datain(regfile_datain), .reg_clk(regfile_clk), .reg_we(decoder_1_out6), .reset(reset),
    .reg_dataout(register_6_reg_dataout));
  register register_7 (
    .reg_datain(regfile_datain), .reg_clk(regfile_clk), .reg_we(decoder_1_out7), .reset(reset),
    .reg_dataout(register_7_reg_dataout));
  // Probe on {16{1'b0}}
  // Probe on register_1_reg_dataout
  // Probe on register_2_reg_dataout
  Multiplexer #(.select(3), .width(16), .disabled("Z"), .enable("false")) multiplexer_1 (
    .in0({16{1'b0}}), .in1(register_1_reg_dataout), .in2(register_2_reg_dataout),
    .in3(register_3_reg_dataout), .in4(register_4_reg_dataout), .in5(register_5_reg_dataout),
    .in6(register_6_reg_dataout), .in7(register_7_reg_dataout), .out(regfile_rs2_out), .sel(regfile_rs2));
  // Probe on register_3_reg_dataout
  Multiplexer #(.select(3), .width(16), .disabled("Z"), .enable("false")) multiplexer_2 (
    .in0({16{1'b0}}), .in1(register_1_reg_dataout), .in2(register_2_reg_dataout),
    .in3(register_3_reg_dataout), .in4(register_4_reg_dataout), .in5(register_5_reg_dataout),
    .in6(register_6_reg_dataout), .in7(register_7_reg_dataout), .out(regfile_rs1_out), .sel(regfile_rs1));
  // Probe on register_4_reg_dataout
  // Probe on register_5_reg_dataout
  // Probe on register_6_reg_dataout
  // Probe on register_7_reg_dataout
endmodule

module onebitadder (
  input  onebitadder_cin,
  input  onebitadder_a,
  input  onebitadder_b,
  output onebitadder_sum,
  output onebitadder_cout
);

  wire and_1_out, and_2_out, xor_1_out;

  xor xor_1 (xor_1_out, onebitadder_a, onebitadder_b);
  and and_1 (and_1_out, onebitadder_cin, xor_1_out);
  and and_2 (and_2_out, onebitadder_b, onebitadder_a);
  xor xor_2 (onebitadder_sum, xor_1_out, onebitadder_cin);
  or or_1 (onebitadder_cout, and_1_out, and_2_out);
endmodule

module sixteenbitadder (
  input  [15:0] sixteenbitadder_b,
  input  sixteenbitadder_op,
  input  [15:0] sixteenbitadder_a,
  output sixteenbitadder_ovf,
  output [15:0] sixteenbitadder_sum
);

  wire onebitadder_1_onebitadder_cout, onebitadder_2_onebitadder_cout, onebitadder_3_onebitadder_cout,
       onebitadder_4_onebitadder_cout, onebitadder_5_onebitadder_cout, onebitadder_6_onebitadder_cout,
       onebitadder_7_onebitadder_cout, onebitadder_8_onebitadder_cout, onebitadder_9_onebitadder_cout,
       onebitadder_10_onebitadder_cout, onebitadder_11_onebitadder_cout, onebitadder_12_onebitadder_cout,
       onebitadder_13_onebitadder_cout, onebitadder_14_onebitadder_cout, onebitadder_15_onebitadder_cout,
       onebitadder_16_onebitadder_cout, xor_1_out, xor_2_out, xor_3_out, xor_4_out, xor_5_out, xor_6_out,
       xor_7_out, xor_8_out, xor_9_out, xor_10_out, xor_11_out, xor_12_out, xor_13_out, xor_14_out,
       xor_15_out, xor_16_out;

  xor xor_1 (xor_1_out, sixteenbitadder_b[0], sixteenbitadder_op);
  onebitadder onebitadder_1 (
    .onebitadder_cin(sixteenbitadder_op), .onebitadder_a(sixteenbitadder_a[0]), .onebitadder_b(xor_1_out),
    .onebitadder_sum(sixteenbitadder_sum[0]), .onebitadder_cout(onebitadder_1_onebitadder_cout));
  xor xor_2 (xor_2_out, sixteenbitadder_b[1], sixteenbitadder_op);
  onebitadder onebitadder_2 (
    .onebitadder_cin(onebitadder_1_onebitadder_cout), .onebitadder_a(sixteenbitadder_a[1]),
    .onebitadder_b(xor_2_out), .onebitadder_sum(sixteenbitadder_sum[1]),
    .onebitadder_cout(onebitadder_2_onebitadder_cout));
  xor xor_3 (xor_3_out, sixteenbitadder_b[2], sixteenbitadder_op);
  onebitadder onebitadder_3 (
    .onebitadder_cin(onebitadder_2_onebitadder_cout), .onebitadder_a(sixteenbitadder_a[2]),
    .onebitadder_b(xor_3_out), .onebitadder_sum(sixteenbitadder_sum[2]),
    .onebitadder_cout(onebitadder_3_onebitadder_cout));
  xor xor_4 (xor_4_out, sixteenbitadder_b[3], sixteenbitadder_op);
  onebitadder onebitadder_4 (
    .onebitadder_cin(onebitadder_3_onebitadder_cout), .onebitadder_a(sixteenbitadder_a[3]),
    .onebitadder_b(xor_4_out), .onebitadder_sum(sixteenbitadder_sum[3]),
    .onebitadder_cout(onebitadder_4_onebitadder_cout));
  xor xor_5 (xor_5_out, sixteenbitadder_b[4], sixteenbitadder_op);
  onebitadder onebitadder_5 (
    .onebitadder_cin(onebitadder_4_onebitadder_cout), .onebitadder_a(sixteenbitadder_a[4]),
    .onebitadder_b(xor_5_out), .onebitadder_sum(sixteenbitadder_sum[4]),
    .onebitadder_cout(onebitadder_5_onebitadder_cout));
  xor xor_6 (xor_6_out, sixteenbitadder_b[5], sixteenbitadder_op);
  onebitadder onebitadder_6 (
    .onebitadder_cin(onebitadder_5_onebitadder_cout), .onebitadder_a(sixteenbitadder_a[5]),
    .onebitadder_b(xor_6_out), .onebitadder_sum(sixteenbitadder_sum[5]),
    .onebitadder_cout(onebitadder_6_onebitadder_cout));
  xor xor_7 (xor_7_out, sixteenbitadder_b[6], sixteenbitadder_op);
  onebitadder onebitadder_7 (
    .onebitadder_cin(onebitadder_6_onebitadder_cout), .onebitadder_a(sixteenbitadder_a[6]),
    .onebitadder_b(xor_7_out), .onebitadder_sum(sixteenbitadder_sum[6]),
    .onebitadder_cout(onebitadder_7_onebitadder_cout));
  xor xor_8 (xor_8_out, sixteenbitadder_b[7], sixteenbitadder_op);
  onebitadder onebitadder_8 (
    .onebitadder_cin(onebitadder_7_onebitadder_cout), .onebitadder_a(sixteenbitadder_a[7]),
    .onebitadder_b(xor_8_out), .onebitadder_sum(sixteenbitadder_sum[7]),
    .onebitadder_cout(onebitadder_8_onebitadder_cout));
  xor xor_9 (xor_9_out, sixteenbitadder_b[8], sixteenbitadder_op);
  onebitadder onebitadder_9 (
    .onebitadder_cin(onebitadder_8_onebitadder_cout), .onebitadder_a(sixteenbitadder_a[8]),
    .onebitadder_b(xor_9_out), .onebitadder_sum(sixteenbitadder_sum[8]),
    .onebitadder_cout(onebitadder_9_onebitadder_cout));
  xor xor_10 (xor_10_out, sixteenbitadder_b[9], sixteenbitadder_op);
  onebitadder onebitadder_10 (
    .onebitadder_cin(onebitadder_9_onebitadder_cout), .onebitadder_a(sixteenbitadder_a[9]),
    .onebitadder_b(xor_10_out), .onebitadder_sum(sixteenbitadder_sum[9]),
    .onebitadder_cout(onebitadder_10_onebitadder_cout));
  xor xor_11 (xor_11_out, sixteenbitadder_b[10], sixteenbitadder_op);
  onebitadder onebitadder_11 (
    .onebitadder_cin(onebitadder_10_onebitadder_cout), .onebitadder_a(sixteenbitadder_a[10]),
    .onebitadder_b(xor_11_out), .onebitadder_sum(sixteenbitadder_sum[10]),
    .onebitadder_cout(onebitadder_11_onebitadder_cout));
  xor xor_12 (xor_12_out, sixteenbitadder_b[11], sixteenbitadder_op);
  onebitadder onebitadder_12 (
    .onebitadder_cin(onebitadder_11_onebitadder_cout), .onebitadder_a(sixteenbitadder_a[11]),
    .onebitadder_b(xor_12_out), .onebitadder_sum(sixteenbitadder_sum[11]),
    .onebitadder_cout(onebitadder_12_onebitadder_cout));
  xor xor_13 (xor_13_out, sixteenbitadder_b[12], sixteenbitadder_op);
  onebitadder onebitadder_13 (
    .onebitadder_cin(onebitadder_12_onebitadder_cout), .onebitadder_a(sixteenbitadder_a[12]),
    .onebitadder_b(xor_13_out), .onebitadder_sum(sixteenbitadder_sum[12]),
    .onebitadder_cout(onebitadder_13_onebitadder_cout));
  xor xor_14 (xor_14_out, sixteenbitadder_b[13], sixteenbitadder_op);
  onebitadder onebitadder_14 (
    .onebitadder_cin(onebitadder_13_onebitadder_cout), .onebitadder_a(sixteenbitadder_a[13]),
    .onebitadder_b(xor_14_out), .onebitadder_sum(sixteenbitadder_sum[13]),
    .onebitadder_cout(onebitadder_14_onebitadder_cout));
  xor xor_15 (xor_15_out, sixteenbitadder_b[14], sixteenbitadder_op);
  onebitadder onebitadder_15 (
    .onebitadder_cin(onebitadder_14_onebitadder_cout), .onebitadder_a(sixteenbitadder_a[14]),
    .onebitadder_b(xor_15_out), .onebitadder_sum(sixteenbitadder_sum[14]),
    .onebitadder_cout(onebitadder_15_onebitadder_cout));
  xor xor_16 (xor_16_out, sixteenbitadder_b[15], sixteenbitadder_op);
  onebitadder onebitadder_16 (
    .onebitadder_cin(onebitadder_15_onebitadder_cout), .onebitadder_a(sixteenbitadder_a[15]),
    .onebitadder_b(xor_16_out), .onebitadder_sum(sixteenbitadder_sum[15]),
    .onebitadder_cout(onebitadder_16_onebitadder_cout));
  xor xor_17 (sixteenbitadder_ovf, onebitadder_15_onebitadder_cout, onebitadder_16_onebitadder_cout);
endmodule

module alu (
  input  [15:0] alu_a,
  input  [15:0] alu_b,
  input  [2:0] alu_muxselector,
  output [15:0] out_4,
  output out_5,
  output a_b
);

  wire [15:0] and_1_out, leftshifter_1_leftshifter_output, or_1_out, rightshifter_1_rightbitshifter_output,
       sixteenbitadder_1_sixteenbitadder_sum, sixteenbitadder_2_sixteenbitadder_sum;

  sixteenbitadder sixteenbitadder_1 (
    .sixteenbitadder_b(alu_b), .sixteenbitadder_a(alu_a),
    .sixteenbitadder_sum(sixteenbitadder_1_sixteenbitadder_sum), .sixteenbitadder_op(1'b0));  // open: sixteenbitadder_ovf
  sixteenbitadder sixteenbitadder_2 (
    .sixteenbitadder_b(alu_b), .sixteenbitadder_a(alu_a),
    .sixteenbitadder_sum(sixteenbitadder_2_sixteenbitadder_sum), .sixteenbitadder_op(1'b1));  // open: sixteenbitadder_ovf
  rightshifter rightshifter_1 (
    .rightbitshifter_input(alu_a), .rightshifter_muxselector(alu_b[2:0]),
    .rightbitshifter_output(rightshifter_1_rightbitshifter_output));
  leftshifter leftshifter_1 (
    .leftshifter_input(alu_a), .leftshifter_muxselector(alu_b[2:0]),
    .leftshifter_output(leftshifter_1_leftshifter_output));
  comparison comparison_1 (.comparison_input_a(alu_a), .comparison_input_b(alu_b), .out_3(a_b));
  assign or_1_out = alu_a | alu_b;  // OR_Gate or_1, 16 bits wide
  assign and_1_out = alu_a & alu_b;  // AND_Gate and_1, 16 bits wide
  Multiplexer #(.select(3), .width(16), .disabled("Z"), .enable("false")) multiplexer_1 (
    .in0(or_1_out), .in1(and_1_out), .in2(sixteenbitadder_1_sixteenbitadder_sum),
    .in3(sixteenbitadder_2_sixteenbitadder_sum), .in4(rightshifter_1_rightbitshifter_output),
    .in5(leftshifter_1_leftshifter_output), .in6(sixteenbitadder_1_sixteenbitadder_sum), .out(out_4),
    .sel(alu_muxselector));  // open: in7
  not not_1 (out_5, sixteenbitadder_2_sixteenbitadder_sum[15]);

  // Notes on the sheet:
  //   right shifter
  //   left shifter
  //   this shows a>b but does not work when a=b
endmodule

module sixteenbitshifter (
  input  sixteenbitshifter_op,
  input  [15:0] sixteenbitshifter_input,
  output [15:0] sixteenbitshifter_output
);

  wire and_1_out, and_3_out, and_4_out, and_5_out, and_6_out, and_7_out, and_8_out, and_9_out, and_10_out,
       and_11_out, and_12_out, and_13_out, and_14_out, and_15_out, and_16_out, and_17_out, and_18_out,
       and_19_out, and_20_out, and_21_out, and_22_out, and_23_out, and_24_out, and_25_out, and_26_out,
       and_27_out, and_28_out, and_30_out, not_1_out;

  not not_1 (not_1_out, sixteenbitshifter_op);
  and and_1 (and_1_out, sixteenbitshifter_input[0], not_1_out);
  and and_2 (sixteenbitshifter_output[0], sixteenbitshifter_op, sixteenbitshifter_input[1]);
  and and_3 (and_3_out, sixteenbitshifter_input[1], not_1_out);
  and and_4 (and_4_out, sixteenbitshifter_op, sixteenbitshifter_input[2]);
  and and_5 (and_5_out, sixteenbitshifter_input[2], not_1_out);
  and and_6 (and_6_out, sixteenbitshifter_op, sixteenbitshifter_input[3]);
  and and_7 (and_7_out, sixteenbitshifter_input[3], not_1_out);
  and and_8 (and_8_out, sixteenbitshifter_op, sixteenbitshifter_input[4]);
  and and_9 (and_9_out, sixteenbitshifter_input[4], not_1_out);
  and and_10 (and_10_out, sixteenbitshifter_op, sixteenbitshifter_input[5]);
  and and_11 (and_11_out, sixteenbitshifter_input[5], not_1_out);
  and and_12 (and_12_out, sixteenbitshifter_op, sixteenbitshifter_input[6]);
  and and_13 (and_13_out, sixteenbitshifter_input[6], not_1_out);
  and and_14 (and_14_out, sixteenbitshifter_op, sixteenbitshifter_input[7]);
  and and_15 (and_15_out, sixteenbitshifter_input[7], not_1_out);
  and and_16 (and_16_out, sixteenbitshifter_op, sixteenbitshifter_input[8]);
  and and_17 (and_17_out, sixteenbitshifter_input[8], not_1_out);
  and and_18 (and_18_out, sixteenbitshifter_op, sixteenbitshifter_input[9]);
  and and_19 (and_19_out, sixteenbitshifter_input[9], not_1_out);
  and and_20 (and_20_out, sixteenbitshifter_op, sixteenbitshifter_input[10]);
  and and_21 (and_21_out, sixteenbitshifter_input[10], not_1_out);
  and and_22 (and_22_out, sixteenbitshifter_op, sixteenbitshifter_input[11]);
  and and_23 (and_23_out, sixteenbitshifter_input[11], not_1_out);
  and and_24 (and_24_out, sixteenbitshifter_op, sixteenbitshifter_input[12]);
  and and_25 (and_25_out, sixteenbitshifter_input[12], not_1_out);
  and and_26 (and_26_out, sixteenbitshifter_op, sixteenbitshifter_input[13]);
  and and_27 (and_27_out, sixteenbitshifter_input[13], not_1_out);
  and and_28 (and_28_out, sixteenbitshifter_op, sixteenbitshifter_input[14]);
  and and_29 (sixteenbitshifter_output[15], sixteenbitshifter_input[14], not_1_out);
  and and_30 (and_30_out, sixteenbitshifter_op, sixteenbitshifter_input[15]);
  or or_1 (sixteenbitshifter_output[1], and_1_out, and_4_out);
  or or_2 (sixteenbitshifter_output[2], and_3_out, and_6_out);
  or or_3 (sixteenbitshifter_output[3], and_5_out, and_8_out);
  or or_4 (sixteenbitshifter_output[4], and_7_out, and_10_out);
  or or_5 (sixteenbitshifter_output[5], and_9_out, and_12_out);
  or or_6 (sixteenbitshifter_output[6], and_11_out, and_14_out);
  or or_7 (sixteenbitshifter_output[7], and_13_out, and_16_out);
  or or_8 (sixteenbitshifter_output[8], and_15_out, and_18_out);
  or or_9 (sixteenbitshifter_output[9], and_17_out, and_20_out);
  or or_10 (sixteenbitshifter_output[10], and_19_out, and_22_out);
  or or_11 (sixteenbitshifter_output[11], and_21_out, and_24_out);
  or or_12 (sixteenbitshifter_output[12], and_23_out, and_26_out);
  or or_13 (sixteenbitshifter_output[13], and_25_out, and_28_out);
  or or_14 (sixteenbitshifter_output[14], and_27_out, and_30_out);
endmodule

module rightshifter (
  input  [15:0] rightbitshifter_input,
  input  [2:0] rightshifter_muxselector,
  output [15:0] rightbitshifter_output
);

  wire decoder_1_out0;
  wire [14:0] sixteenbitshifter_54_sixteenbitshifter_output_2;
  wire [15:0] buffer_1_out, buffer_2_out, multiplexer_1_out, multiplexer_2_out,
       sixteenbitshifter_1_sixteenbitshifter_output, sixteenbitshifter_2_sixteenbitshifter_output,
       sixteenbitshifter_3_sixteenbitshifter_output, sixteenbitshifter_4_sixteenbitshifter_output,
       sixteenbitshifter_5_sixteenbitshifter_output, sixteenbitshifter_6_sixteenbitshifter_output,
       sixteenbitshifter_7_sixteenbitshifter_output, sixteenbitshifter_8_sixteenbitshifter_output,
       sixteenbitshifter_9_sixteenbitshifter_output, sixteenbitshifter_10_sixteenbitshifter_output,
       sixteenbitshifter_11_sixteenbitshifter_output, sixteenbitshifter_12_sixteenbitshifter_output,
       sixteenbitshifter_13_sixteenbitshifter_output, sixteenbitshifter_14_sixteenbitshifter_output,
       sixteenbitshifter_15_sixteenbitshifter_output, sixteenbitshifter_16_sixteenbitshifter_output,
       sixteenbitshifter_17_sixteenbitshifter_output, sixteenbitshifter_18_sixteenbitshifter_output,
       sixteenbitshifter_19_sixteenbitshifter_output, sixteenbitshifter_20_sixteenbitshifter_output,
       sixteenbitshifter_21_sixteenbitshifter_output, sixteenbitshifter_22_sixteenbitshifter_output,
       sixteenbitshifter_23_sixteenbitshifter_output, sixteenbitshifter_24_sixteenbitshifter_output,
       sixteenbitshifter_25_sixteenbitshifter_output, sixteenbitshifter_26_sixteenbitshifter_output,
       sixteenbitshifter_27_sixteenbitshifter_output, sixteenbitshifter_28_sixteenbitshifter_output,
       sixteenbitshifter_29_sixteenbitshifter_output, sixteenbitshifter_30_sixteenbitshifter_output,
       sixteenbitshifter_31_sixteenbitshifter_output, sixteenbitshifter_32_sixteenbitshifter_output,
       sixteenbitshifter_33_sixteenbitshifter_output, sixteenbitshifter_34_sixteenbitshifter_output,
       sixteenbitshifter_35_sixteenbitshifter_output, sixteenbitshifter_36_sixteenbitshifter_output,
       sixteenbitshifter_37_sixteenbitshifter_output, sixteenbitshifter_38_sixteenbitshifter_output,
       sixteenbitshifter_39_sixteenbitshifter_output, sixteenbitshifter_40_sixteenbitshifter_output,
       sixteenbitshifter_41_sixteenbitshifter_output, sixteenbitshifter_42_sixteenbitshifter_output,
       sixteenbitshifter_43_sixteenbitshifter_output, sixteenbitshifter_44_sixteenbitshifter_output,
       sixteenbitshifter_45_sixteenbitshifter_output, sixteenbitshifter_46_sixteenbitshifter_output,
       sixteenbitshifter_47_sixteenbitshifter_output, sixteenbitshifter_48_sixteenbitshifter_output,
       sixteenbitshifter_49_sixteenbitshifter_output, sixteenbitshifter_50_sixteenbitshifter_output,
       sixteenbitshifter_51_sixteenbitshifter_output, sixteenbitshifter_52_sixteenbitshifter_output,
       sixteenbitshifter_53_sixteenbitshifter_output, sixteenbitshifter_55_sixteenbitshifter_output,
       sixteenbitshifter_56_sixteenbitshifter_output;
  wire [15:15] decoder_1_out1, not_1_out, not_2_out, not_3_out, not_4_out, not_5_out, not_6_out, not_7_out,
       not_8_out, not_9_out, not_10_out, not_11_out, not_12_out, not_13_out, not_14_out, not_15_out,
       not_16_out, not_17_out, not_18_out, not_19_out, not_20_out, not_21_out, not_22_out, not_23_out,
       not_24_out, not_25_out, not_26_out, not_27_out, not_28_out, not_29_out,
       sixteenbitshifter_54_sixteenbitshifter_output;

  Decoder decoder_1 (.out0(decoder_1_out0), .out1(decoder_1_out1[15]), .sel(rightbitshifter_input[15]), .en(1'b1));
  not not_1 (not_1_out[15], decoder_1_out0);
  assign buffer_1_out = {decoder_1_out1[15], rightbitshifter_input[14:0]};  // Buffer buffer_1, 16 bits wide
  sixteenbitshifter sixteenbitshifter_1 (
    .sixteenbitshifter_op(1'b1), .sixteenbitshifter_input({decoder_1_out1[15], rightbitshifter_input[14:0]}),
    .sixteenbitshifter_output(sixteenbitshifter_1_sixteenbitshifter_output));
  sixteenbitshifter sixteenbitshifter_2 (
    .sixteenbitshifter_op(1'b1), .sixteenbitshifter_input({decoder_1_out1[15], rightbitshifter_input[14:0]}),
    .sixteenbitshifter_output(sixteenbitshifter_2_sixteenbitshifter_output));
  sixteenbitshifter sixteenbitshifter_3 (
    .sixteenbitshifter_op(1'b1), .sixteenbitshifter_input({decoder_1_out1[15], rightbitshifter_input[14:0]}),
    .sixteenbitshifter_output(sixteenbitshifter_3_sixteenbitshifter_output));
  sixteenbitshifter sixteenbitshifter_4 (
    .sixteenbitshifter_op(1'b1), .sixteenbitshifter_input({decoder_1_out1[15], rightbitshifter_input[14:0]}),
    .sixteenbitshifter_output(sixteenbitshifter_4_sixteenbitshifter_output));
  sixteenbitshifter sixteenbitshifter_5 (
    .sixteenbitshifter_op(1'b1), .sixteenbitshifter_input({decoder_1_out1[15], rightbitshifter_input[14:0]}),
    .sixteenbitshifter_output(sixteenbitshifter_5_sixteenbitshifter_output));
  sixteenbitshifter sixteenbitshifter_6 (
    .sixteenbitshifter_op(1'b1), .sixteenbitshifter_input({decoder_1_out1[15], rightbitshifter_input[14:0]}),
    .sixteenbitshifter_output(sixteenbitshifter_6_sixteenbitshifter_output));
  sixteenbitshifter sixteenbitshifter_7 (
    .sixteenbitshifter_op(1'b1), .sixteenbitshifter_input({decoder_1_out1[15], rightbitshifter_input[14:0]}),
    .sixteenbitshifter_output(sixteenbitshifter_7_sixteenbitshifter_output));
  assign buffer_2_out = {not_1_out[15], rightbitshifter_input[14:0]};  // Buffer buffer_2, 16 bits wide
  sixteenbitshifter sixteenbitshifter_8 (
    .sixteenbitshifter_op(1'b1), .sixteenbitshifter_input({not_1_out[15], rightbitshifter_input[14:0]}),
    .sixteenbitshifter_output(sixteenbitshifter_8_sixteenbitshifter_output));
  sixteenbitshifter sixteenbitshifter_9 (
    .sixteenbitshifter_op(1'b1), .sixteenbitshifter_input({not_1_out[15], rightbitshifter_input[14:0]}),
    .sixteenbitshifter_output(sixteenbitshifter_9_sixteenbitshifter_output));
  sixteenbitshifter sixteenbitshifter_10 (
    .sixteenbitshifter_op(1'b1), .sixteenbitshifter_input({not_1_out[15], rightbitshifter_input[14:0]}),
    .sixteenbitshifter_output(sixteenbitshifter_10_sixteenbitshifter_output));
  sixteenbitshifter sixteenbitshifter_11 (
    .sixteenbitshifter_op(1'b1), .sixteenbitshifter_input({not_1_out[15], rightbitshifter_input[14:0]}),
    .sixteenbitshifter_output(sixteenbitshifter_11_sixteenbitshifter_output));
  sixteenbitshifter sixteenbitshifter_12 (
    .sixteenbitshifter_op(1'b1), .sixteenbitshifter_input({not_1_out[15], rightbitshifter_input[14:0]}),
    .sixteenbitshifter_output(sixteenbitshifter_12_sixteenbitshifter_output));
  sixteenbitshifter sixteenbitshifter_13 (
    .sixteenbitshifter_op(1'b1), .sixteenbitshifter_input({not_1_out[15], rightbitshifter_input[14:0]}),
    .sixteenbitshifter_output(sixteenbitshifter_13_sixteenbitshifter_output));
  sixteenbitshifter sixteenbitshifter_14 (
    .sixteenbitshifter_op(1'b1), .sixteenbitshifter_input({not_1_out[15], rightbitshifter_input[14:0]}),
    .sixteenbitshifter_output(sixteenbitshifter_14_sixteenbitshifter_output));
  not not_2 (not_2_out[15], sixteenbitshifter_1_sixteenbitshifter_output[15]);
  not not_3 (not_3_out[15], sixteenbitshifter_2_sixteenbitshifter_output[15]);
  not not_4 (not_4_out[15], sixteenbitshifter_3_sixteenbitshifter_output[15]);
  not not_5 (not_5_out[15], sixteenbitshifter_4_sixteenbitshifter_output[15]);
  not not_6 (not_6_out[15], sixteenbitshifter_5_sixteenbitshifter_output[15]);
  not not_7 (not_7_out[15], sixteenbitshifter_6_sixteenbitshifter_output[15]);
  not not_8 (not_8_out[15], sixteenbitshifter_7_sixteenbitshifter_output[15]);
  sixteenbitshifter sixteenbitshifter_15 (
    .sixteenbitshifter_op(1'b1), .sixteenbitshifter_input(sixteenbitshifter_9_sixteenbitshifter_output),
    .sixteenbitshifter_output(sixteenbitshifter_15_sixteenbitshifter_output));
  sixteenbitshifter sixteenbitshifter_16 (
    .sixteenbitshifter_op(1'b1), .sixteenbitshifter_input(sixteenbitshifter_10_sixteenbitshifter_output),
    .sixteenbitshifter_output(sixteenbitshifter_16_sixteenbitshifter_output));
  sixteenbitshifter sixteenbitshifter_17 (
    .sixteenbitshifter_op(1'b1), .sixteenbitshifter_input(sixteenbitshifter_11_sixteenbitshifter_output),
    .sixteenbitshifter_output(sixteenbitshifter_17_sixteenbitshifter_output));
  sixteenbitshifter sixteenbitshifter_18 (
    .sixteenbitshifter_op(1'b1), .sixteenbitshifter_input(sixteenbitshifter_12_sixteenbitshifter_output),
    .sixteenbitshifter_output(sixteenbitshifter_18_sixteenbitshifter_output));
  sixteenbitshifter sixteenbitshifter_19 (
    .sixteenbitshifter_op(1'b1), .sixteenbitshifter_input(sixteenbitshifter_13_sixteenbitshifter_output),
    .sixteenbitshifter_output(sixteenbitshifter_19_sixteenbitshifter_output));
  sixteenbitshifter sixteenbitshifter_20 (
    .sixteenbitshifter_op(1'b1), .sixteenbitshifter_input(sixteenbitshifter_14_sixteenbitshifter_output),
    .sixteenbitshifter_output(sixteenbitshifter_20_sixteenbitshifter_output));
  not not_9 (not_9_out[15], sixteenbitshifter_21_sixteenbitshifter_output[15]);
  sixteenbitshifter sixteenbitshifter_21 (
    .sixteenbitshifter_op(1'b1),
    .sixteenbitshifter_input({not_3_out[15], sixteenbitshifter_2_sixteenbitshifter_output[14:0]}),
    .sixteenbitshifter_output(sixteenbitshifter_21_sixteenbitshifter_output));
  not not_10 (not_10_out[15], sixteenbitshifter_22_sixteenbitshifter_output[15]);
  sixteenbitshifter sixteenbitshifter_22 (
    .sixteenbitshifter_op(1'b1),
    .sixteenbitshifter_input({not_4_out[15], sixteenbitshifter_3_sixteenbitshifter_output[14:0]}),
    .sixteenbitshifter_output(sixteenbitshifter_22_sixteenbitshifter_output));
  not not_11 (not_11_out[15], sixteenbitshifter_23_sixteenbitshifter_output[15]);
  sixteenbitshifter sixteenbitshifter_23 (
    .sixteenbitshifter_op(1'b1),
    .sixteenbitshifter_input({not_5_out[15], sixteenbitshifter_4_sixteenbitshifter_output[14:0]}),
    .sixteenbitshifter_output(sixteenbitshifter_23_sixteenbitshifter_output));
  not not_12 (not_12_out[15], sixteenbitshifter_24_sixteenbitshifter_output[15]);
  sixteenbitshifter sixteenbitshifter_24 (
    .sixteenbitshifter_op(1'b1),
    .sixteenbitshifter_input({not_6_out[15], sixteenbitshifter_5_sixteenbitshifter_output[14:0]}),
    .sixteenbitshifter_output(sixteenbitshifter_24_sixteenbitshifter_output));
  not not_13 (not_13_out[15], sixteenbitshifter_25_sixteenbitshifter_output[15]);
  sixteenbitshifter sixteenbitshifter_25 (
    .sixteenbitshifter_op(1'b1),
    .sixteenbitshifter_input({not_7_out[15], sixteenbitshifter_6_sixteenbitshifter_output[14:0]}),
    .sixteenbitshifter_output(sixteenbitshifter_25_sixteenbitshifter_output));
  not not_14 (not_14_out[15], sixteenbitshifter_26_sixteenbitshifter_output[15]);
  sixteenbitshifter sixteenbitshifter_26 (
    .sixteenbitshifter_op(1'b1),
    .sixteenbitshifter_input({not_8_out[15], sixteenbitshifter_7_sixteenbitshifter_output[14:0]}),
    .sixteenbitshifter_output(sixteenbitshifter_26_sixteenbitshifter_output));
  sixteenbitshifter sixteenbitshifter_27 (
    .sixteenbitshifter_op(1'b1), .sixteenbitshifter_input(sixteenbitshifter_16_sixteenbitshifter_output),
    .sixteenbitshifter_output(sixteenbitshifter_27_sixteenbitshifter_output));
  sixteenbitshifter sixteenbitshifter_28 (
    .sixteenbitshifter_op(1'b1), .sixteenbitshifter_input(sixteenbitshifter_17_sixteenbitshifter_output),
    .sixteenbitshifter_output(sixteenbitshifter_28_sixteenbitshifter_output));
  sixteenbitshifter sixteenbitshifter_29 (
    .sixteenbitshifter_op(1'b1), .sixteenbitshifter_input(sixteenbitshifter_18_sixteenbitshifter_output),
    .sixteenbitshifter_output(sixteenbitshifter_29_sixteenbitshifter_output));
  sixteenbitshifter sixteenbitshifter_30 (
    .sixteenbitshifter_op(1'b1), .sixteenbitshifter_input(sixteenbitshifter_19_sixteenbitshifter_output),
    .sixteenbitshifter_output(sixteenbitshifter_30_sixteenbitshifter_output));
  sixteenbitshifter sixteenbitshifter_31 (
    .sixteenbitshifter_op(1'b1), .sixteenbitshifter_input(sixteenbitshifter_20_sixteenbitshifter_output),
    .sixteenbitshifter_output(sixteenbitshifter_31_sixteenbitshifter_output));
  sixteenbitshifter sixteenbitshifter_32 (
    .sixteenbitshifter_op(1'b1),
    .sixteenbitshifter_input({not_10_out[15], sixteenbitshifter_22_sixteenbitshifter_output[14:0]}),
    .sixteenbitshifter_output(sixteenbitshifter_32_sixteenbitshifter_output));
  sixteenbitshifter sixteenbitshifter_33 (
    .sixteenbitshifter_op(1'b1),
    .sixteenbitshifter_input({not_11_out[15], sixteenbitshifter_23_sixteenbitshifter_output[14:0]}),
    .sixteenbitshifter_output(sixteenbitshifter_33_sixteenbitshifter_output));
  sixteenbitshifter sixteenbitshifter_34 (
    .sixteenbitshifter_op(1'b1),
    .sixteenbitshifter_input({not_12_out[15], sixteenbitshifter_24_sixteenbitshifter_output[14:0]}),
    .sixteenbitshifter_output(sixteenbitshifter_34_sixteenbitshifter_output));
  sixteenbitshifter sixteenbitshifter_35 (
    .sixteenbitshifter_op(1'b1),
    .sixteenbitshifter_input({not_13_out[15], sixteenbitshifter_25_sixteenbitshifter_output[14:0]}),
    .sixteenbitshifter_output(sixteenbitshifter_35_sixteenbitshifter_output));
  sixteenbitshifter sixteenbitshifter_36 (
    .sixteenbitshifter_op(1'b1),
    .sixteenbitshifter_input({not_14_out[15], sixteenbitshifter_26_sixteenbitshifter_output[14:0]}),
    .sixteenbitshifter_output(sixteenbitshifter_36_sixteenbitshifter_output));
  sixteenbitshifter sixteenbitshifter_37 (
    .sixteenbitshifter_op(1'b1), .sixteenbitshifter_input(sixteenbitshifter_28_sixteenbitshifter_output),
    .sixteenbitshifter_output(sixteenbitshifter_37_sixteenbitshifter_output));
  sixteenbitshifter sixteenbitshifter_38 (
    .sixteenbitshifter_op(1'b1), .sixteenbitshifter_input(sixteenbitshifter_29_sixteenbitshifter_output),
    .sixteenbitshifter_output(sixteenbitshifter_38_sixteenbitshifter_output));
  sixteenbitshifter sixteenbitshifter_39 (
    .sixteenbitshifter_op(1'b1), .sixteenbitshifter_input(sixteenbitshifter_30_sixteenbitshifter_output),
    .sixteenbitshifter_output(sixteenbitshifter_39_sixteenbitshifter_output));
  sixteenbitshifter sixteenbitshifter_40 (
    .sixteenbitshifter_op(1'b1), .sixteenbitshifter_input(sixteenbitshifter_31_sixteenbitshifter_output),
    .sixteenbitshifter_output(sixteenbitshifter_40_sixteenbitshifter_output));
  not not_15 (not_15_out[15], sixteenbitshifter_32_sixteenbitshifter_output[15]);
  sixteenbitshifter sixteenbitshifter_41 (
    .sixteenbitshifter_op(1'b1),
    .sixteenbitshifter_input({not_16_out[15], sixteenbitshifter_33_sixteenbitshifter_output[14:0]}),
    .sixteenbitshifter_output(sixteenbitshifter_41_sixteenbitshifter_output));
  not not_16 (not_16_out[15], sixteenbitshifter_33_sixteenbitshifter_output[15]);
  sixteenbitshifter sixteenbitshifter_42 (
    .sixteenbitshifter_op(1'b1),
    .sixteenbitshifter_input({not_17_out[15], sixteenbitshifter_34_sixteenbitshifter_output[14:0]}),
    .sixteenbitshifter_output(sixteenbitshifter_42_sixteenbitshifter_output));
  not not_17 (not_17_out[15], sixteenbitshifter_34_sixteenbitshifter_output[15]);
  sixteenbitshifter sixteenbitshifter_43 (
    .sixteenbitshifter_op(1'b1),
    .sixteenbitshifter_input({not_18_out[15], sixteenbitshifter_35_sixteenbitshifter_output[14:0]}),
    .sixteenbitshifter_output(sixteenbitshifter_43_sixteenbitshifter_output));
  not not_18 (not_18_out[15], sixteenbitshifter_35_sixteenbitshifter_output[15]);
  sixteenbitshifter sixteenbitshifter_44 (
    .sixteenbitshifter_op(1'b1),
    .sixteenbitshifter_input({not_19_out[15], sixteenbitshifter_36_sixteenbitshifter_output[14:0]}),
    .sixteenbitshifter_output(sixteenbitshifter_44_sixteenbitshifter_output));
  not not_19 (not_19_out[15], sixteenbitshifter_36_sixteenbitshifter_output[15]);
  sixteenbitshifter sixteenbitshifter_45 (
    .sixteenbitshifter_op(1'b1), .sixteenbitshifter_input(sixteenbitshifter_38_sixteenbitshifter_output),
    .sixteenbitshifter_output(sixteenbitshifter_45_sixteenbitshifter_output));
  sixteenbitshifter sixteenbitshifter_46 (
    .sixteenbitshifter_op(1'b1), .sixteenbitshifter_input(sixteenbitshifter_39_sixteenbitshifter_output),
    .sixteenbitshifter_output(sixteenbitshifter_46_sixteenbitshifter_output));
  sixteenbitshifter sixteenbitshifter_47 (
    .sixteenbitshifter_op(1'b1), .sixteenbitshifter_input(sixteenbitshifter_40_sixteenbitshifter_output),
    .sixteenbitshifter_output(sixteenbitshifter_47_sixteenbitshifter_output));
  not not_20 (not_20_out[15], sixteenbitshifter_41_sixteenbitshifter_output[15]);
  not not_21 (not_21_out[15], sixteenbitshifter_42_sixteenbitshifter_output[15]);
  not not_22 (not_22_out[15], sixteenbitshifter_43_sixteenbitshifter_output[15]);
  not not_23 (not_23_out[15], sixteenbitshifter_44_sixteenbitshifter_output[15]);
  sixteenbitshifter sixteenbitshifter_48 (
    .sixteenbitshifter_op(1'b1), .sixteenbitshifter_input(sixteenbitshifter_46_sixteenbitshifter_output),
    .sixteenbitshifter_output(sixteenbitshifter_48_sixteenbitshifter_output));
  sixteenbitshifter sixteenbitshifter_49 (
    .sixteenbitshifter_op(1'b1), .sixteenbitshifter_input(sixteenbitshifter_47_sixteenbitshifter_output),
    .sixteenbitshifter_output(sixteenbitshifter_49_sixteenbitshifter_output));
  not not_24 (not_24_out[15], sixteenbitshifter_50_sixteenbitshifter_output[15]);
  sixteenbitshifter sixteenbitshifter_50 (
    .sixteenbitshifter_op(1'b1),
    .sixteenbitshifter_input({not_21_out[15], sixteenbitshifter_42_sixteenbitshifter_output[14:0]}),
    .sixteenbitshifter_output(sixteenbitshifter_50_sixteenbitshifter_output));
  not not_25 (not_25_out[15], sixteenbitshifter_51_sixteenbitshifter_output[15]);
  sixteenbitshifter sixteenbitshifter_51 (
    .sixteenbitshifter_op(1'b1),
    .sixteenbitshifter_input({not_22_out[15], sixteenbitshifter_43_sixteenbitshifter_output[14:0]}),
    .sixteenbitshifter_output(sixteenbitshifter_51_sixteenbitshifter_output));
  not not_26 (not_26_out[15], sixteenbitshifter_52_sixteenbitshifter_output[15]);
  sixteenbitshifter sixteenbitshifter_52 (
    .sixteenbitshifter_op(1'b1),
    .sixteenbitshifter_input({not_23_out[15], sixteenbitshifter_44_sixteenbitshifter_output[14:0]}),
    .sixteenbitshifter_output(sixteenbitshifter_52_sixteenbitshifter_output));
  sixteenbitshifter sixteenbitshifter_53 (
    .sixteenbitshifter_op(1'b1), .sixteenbitshifter_input(sixteenbitshifter_49_sixteenbitshifter_output),
    .sixteenbitshifter_output(sixteenbitshifter_53_sixteenbitshifter_output));
  not not_27 (not_27_out[15], sixteenbitshifter_54_sixteenbitshifter_output[15]);
  sixteenbitshifter sixteenbitshifter_54 (
    .sixteenbitshifter_op(1'b1),
    .sixteenbitshifter_input({not_25_out[15], sixteenbitshifter_51_sixteenbitshifter_output[14:0]}),
    .sixteenbitshifter_output({sixteenbitshifter_54_sixteenbitshifter_output[15], sixteenbitshifter_54_sixteenbitshifter_output_2}));
  sixteenbitshifter sixteenbitshifter_55 (
    .sixteenbitshifter_op(1'b1),
    .sixteenbitshifter_input({not_26_out[15], sixteenbitshifter_52_sixteenbitshifter_output[14:0]}),
    .sixteenbitshifter_output(sixteenbitshifter_55_sixteenbitshifter_output));
  sixteenbitshifter sixteenbitshifter_56 (
    .sixteenbitshifter_op(1'b1),
    .sixteenbitshifter_input({not_28_out[15], sixteenbitshifter_55_sixteenbitshifter_output[14:0]}),
    .sixteenbitshifter_output(sixteenbitshifter_56_sixteenbitshifter_output));
  not not_28 (not_28_out[15], sixteenbitshifter_55_sixteenbitshifter_output[15]);
  Multiplexer #(.select(3), .width(16), .disabled("Z"), .enable("false")) multiplexer_1 (
    .in0(buffer_2_out), .in1(sixteenbitshifter_8_sixteenbitshifter_output),
    .in2(sixteenbitshifter_15_sixteenbitshifter_output), .in3(sixteenbitshifter_27_sixteenbitshifter_output),
    .in4(sixteenbitshifter_37_sixteenbitshifter_output), .in5(sixteenbitshifter_45_sixteenbitshifter_output),
    .in6(sixteenbitshifter_48_sixteenbitshifter_output), .in7(sixteenbitshifter_53_sixteenbitshifter_output),
    .out(multiplexer_1_out), .sel(rightshifter_muxselector));
  not not_29 (not_29_out[15], sixteenbitshifter_56_sixteenbitshifter_output[15]);
  Multiplexer #(.select(3), .width(16), .disabled("Z"), .enable("false")) multiplexer_2 (
    .in0(buffer_1_out), .in1({not_2_out[15], sixteenbitshifter_1_sixteenbitshifter_output[14:0]}),
    .in2({not_9_out[15], sixteenbitshifter_21_sixteenbitshifter_output[14:0]}),
    .in3({not_15_out[15], sixteenbitshifter_32_sixteenbitshifter_output[14:0]}),
    .in4({not_20_out[15], sixteenbitshifter_41_sixteenbitshifter_output[14:0]}),
    .in5({not_24_out[15], sixteenbitshifter_50_sixteenbitshifter_output[14:0]}),
    .in6({not_27_out[15], sixteenbitshifter_54_sixteenbitshifter_output_2}),
    .in7({not_29_out[15], sixteenbitshifter_56_sixteenbitshifter_output[14:0]}), .out(multiplexer_2_out),
    .sel(rightshifter_muxselector));
  Multiplexer #(.width(16), .disabled("Z"), .enable("false")) multiplexer_3 (
    .in0(multiplexer_1_out), .in1(multiplexer_2_out), .out(rightbitshifter_output),
    .sel(rightbitshifter_input[15]));
endmodule

module leftshifter (
  input  [15:0] leftshifter_input,
  input  [2:0] leftshifter_muxselector,
  output [15:0] leftshifter_output
);

  wire [15:0] buffer_1_out, sixteenbitshifter_1_sixteenbitshifter_output,
       sixteenbitshifter_2_sixteenbitshifter_output, sixteenbitshifter_3_sixteenbitshifter_output,
       sixteenbitshifter_4_sixteenbitshifter_output, sixteenbitshifter_5_sixteenbitshifter_output,
       sixteenbitshifter_6_sixteenbitshifter_output, sixteenbitshifter_7_sixteenbitshifter_output,
       sixteenbitshifter_8_sixteenbitshifter_output, sixteenbitshifter_9_sixteenbitshifter_output,
       sixteenbitshifter_10_sixteenbitshifter_output, sixteenbitshifter_11_sixteenbitshifter_output,
       sixteenbitshifter_12_sixteenbitshifter_output, sixteenbitshifter_13_sixteenbitshifter_output,
       sixteenbitshifter_14_sixteenbitshifter_output, sixteenbitshifter_15_sixteenbitshifter_output,
       sixteenbitshifter_16_sixteenbitshifter_output, sixteenbitshifter_17_sixteenbitshifter_output,
       sixteenbitshifter_18_sixteenbitshifter_output, sixteenbitshifter_19_sixteenbitshifter_output,
       sixteenbitshifter_20_sixteenbitshifter_output, sixteenbitshifter_21_sixteenbitshifter_output,
       sixteenbitshifter_22_sixteenbitshifter_output, sixteenbitshifter_23_sixteenbitshifter_output,
       sixteenbitshifter_24_sixteenbitshifter_output, sixteenbitshifter_25_sixteenbitshifter_output,
       sixteenbitshifter_26_sixteenbitshifter_output, sixteenbitshifter_27_sixteenbitshifter_output,
       sixteenbitshifter_28_sixteenbitshifter_output;

  assign buffer_1_out = leftshifter_input;  // Buffer buffer_1, 16 bits wide
  sixteenbitshifter sixteenbitshifter_1 (
    .sixteenbitshifter_op(1'b0), .sixteenbitshifter_input(leftshifter_input),
    .sixteenbitshifter_output(sixteenbitshifter_1_sixteenbitshifter_output));
  sixteenbitshifter sixteenbitshifter_2 (
    .sixteenbitshifter_op(1'b0), .sixteenbitshifter_input(leftshifter_input),
    .sixteenbitshifter_output(sixteenbitshifter_2_sixteenbitshifter_output));
  sixteenbitshifter sixteenbitshifter_3 (
    .sixteenbitshifter_op(1'b0), .sixteenbitshifter_input(leftshifter_input),
    .sixteenbitshifter_output(sixteenbitshifter_3_sixteenbitshifter_output));
  sixteenbitshifter sixteenbitshifter_4 (
    .sixteenbitshifter_op(1'b0), .sixteenbitshifter_input(leftshifter_input),
    .sixteenbitshifter_output(sixteenbitshifter_4_sixteenbitshifter_output));
  sixteenbitshifter sixteenbitshifter_5 (
    .sixteenbitshifter_op(1'b0), .sixteenbitshifter_input(leftshifter_input),
    .sixteenbitshifter_output(sixteenbitshifter_5_sixteenbitshifter_output));
  sixteenbitshifter sixteenbitshifter_6 (
    .sixteenbitshifter_op(1'b0), .sixteenbitshifter_input(leftshifter_input),
    .sixteenbitshifter_output(sixteenbitshifter_6_sixteenbitshifter_output));
  sixteenbitshifter sixteenbitshifter_7 (
    .sixteenbitshifter_op(1'b0), .sixteenbitshifter_input(leftshifter_input),
    .sixteenbitshifter_output(sixteenbitshifter_7_sixteenbitshifter_output));
  sixteenbitshifter sixteenbitshifter_8 (
    .sixteenbitshifter_op(1'b0), .sixteenbitshifter_input(sixteenbitshifter_2_sixteenbitshifter_output),
    .sixteenbitshifter_output(sixteenbitshifter_8_sixteenbitshifter_output));
  sixteenbitshifter sixteenbitshifter_9 (
    .sixteenbitshifter_op(1'b0), .sixteenbitshifter_input(sixteenbitshifter_3_sixteenbitshifter_output),
    .sixteenbitshifter_output(sixteenbitshifter_9_sixteenbitshifter_output));
  sixteenbitshifter sixteenbitshifter_10 (
    .sixteenbitshifter_op(1'b0), .sixteenbitshifter_input(sixteenbitshifter_4_sixteenbitshifter_output),
    .sixteenbitshifter_output(sixteenbitshifter_10_sixteenbitshifter_output));
  sixteenbitshifter sixteenbitshifter_11 (
    .sixteenbitshifter_op(1'b0), .sixteenbitshifter_input(sixteenbitshifter_5_sixteenbitshifter_output),
    .sixteenbitshifter_output(sixteenbitshifter_11_sixteenbitshifter_output));
  sixteenbitshifter sixteenbitshifter_12 (
    .sixteenbitshifter_op(1'b0), .sixteenbitshifter_input(sixteenbitshifter_6_sixteenbitshifter_output),
    .sixteenbitshifter_output(sixteenbitshifter_12_sixteenbitshifter_output));
  sixteenbitshifter sixteenbitshifter_13 (
    .sixteenbitshifter_op(1'b0), .sixteenbitshifter_input(sixteenbitshifter_7_sixteenbitshifter_output),
    .sixteenbitshifter_output(sixteenbitshifter_13_sixteenbitshifter_output));
  sixteenbitshifter sixteenbitshifter_14 (
    .sixteenbitshifter_op(1'b0), .sixteenbitshifter_input(sixteenbitshifter_9_sixteenbitshifter_output),
    .sixteenbitshifter_output(sixteenbitshifter_14_sixteenbitshifter_output));
  sixteenbitshifter sixteenbitshifter_15 (
    .sixteenbitshifter_op(1'b0), .sixteenbitshifter_input(sixteenbitshifter_10_sixteenbitshifter_output),
    .sixteenbitshifter_output(sixteenbitshifter_15_sixteenbitshifter_output));
  sixteenbitshifter sixteenbitshifter_16 (
    .sixteenbitshifter_op(1'b0), .sixteenbitshifter_input(sixteenbitshifter_11_sixteenbitshifter_output),
    .sixteenbitshifter_output(sixteenbitshifter_16_sixteenbitshifter_output));
  sixteenbitshifter sixteenbitshifter_17 (
    .sixteenbitshifter_op(1'b0), .sixteenbitshifter_input(sixteenbitshifter_12_sixteenbitshifter_output),
    .sixteenbitshifter_output(sixteenbitshifter_17_sixteenbitshifter_output));
  sixteenbitshifter sixteenbitshifter_18 (
    .sixteenbitshifter_op(1'b0), .sixteenbitshifter_input(sixteenbitshifter_13_sixteenbitshifter_output),
    .sixteenbitshifter_output(sixteenbitshifter_18_sixteenbitshifter_output));
  sixteenbitshifter sixteenbitshifter_19 (
    .sixteenbitshifter_op(1'b0), .sixteenbitshifter_input(sixteenbitshifter_15_sixteenbitshifter_output),
    .sixteenbitshifter_output(sixteenbitshifter_19_sixteenbitshifter_output));
  sixteenbitshifter sixteenbitshifter_20 (
    .sixteenbitshifter_op(1'b0), .sixteenbitshifter_input(sixteenbitshifter_16_sixteenbitshifter_output),
    .sixteenbitshifter_output(sixteenbitshifter_20_sixteenbitshifter_output));
  sixteenbitshifter sixteenbitshifter_21 (
    .sixteenbitshifter_op(1'b0), .sixteenbitshifter_input(sixteenbitshifter_17_sixteenbitshifter_output),
    .sixteenbitshifter_output(sixteenbitshifter_21_sixteenbitshifter_output));
  sixteenbitshifter sixteenbitshifter_22 (
    .sixteenbitshifter_op(1'b0), .sixteenbitshifter_input(sixteenbitshifter_18_sixteenbitshifter_output),
    .sixteenbitshifter_output(sixteenbitshifter_22_sixteenbitshifter_output));
  sixteenbitshifter sixteenbitshifter_23 (
    .sixteenbitshifter_op(1'b0), .sixteenbitshifter_input(sixteenbitshifter_20_sixteenbitshifter_output),
    .sixteenbitshifter_output(sixteenbitshifter_23_sixteenbitshifter_output));
  sixteenbitshifter sixteenbitshifter_24 (
    .sixteenbitshifter_op(1'b0), .sixteenbitshifter_input(sixteenbitshifter_21_sixteenbitshifter_output),
    .sixteenbitshifter_output(sixteenbitshifter_24_sixteenbitshifter_output));
  sixteenbitshifter sixteenbitshifter_25 (
    .sixteenbitshifter_op(1'b0), .sixteenbitshifter_input(sixteenbitshifter_22_sixteenbitshifter_output),
    .sixteenbitshifter_output(sixteenbitshifter_25_sixteenbitshifter_output));
  sixteenbitshifter sixteenbitshifter_26 (
    .sixteenbitshifter_op(1'b0), .sixteenbitshifter_input(sixteenbitshifter_24_sixteenbitshifter_output),
    .sixteenbitshifter_output(sixteenbitshifter_26_sixteenbitshifter_output));
  sixteenbitshifter sixteenbitshifter_27 (
    .sixteenbitshifter_op(1'b0), .sixteenbitshifter_input(sixteenbitshifter_25_sixteenbitshifter_output),
    .sixteenbitshifter_output(sixteenbitshifter_27_sixteenbitshifter_output));
  sixteenbitshifter sixteenbitshifter_28 (
    .sixteenbitshifter_op(1'b0), .sixteenbitshifter_input(sixteenbitshifter_27_sixteenbitshifter_output),
    .sixteenbitshifter_output(sixteenbitshifter_28_sixteenbitshifter_output));
  Multiplexer #(.select(3), .width(16), .disabled("Z"), .enable("false")) multiplexer_1 (
    .in0(buffer_1_out), .in1(sixteenbitshifter_1_sixteenbitshifter_output),
    .in2(sixteenbitshifter_8_sixteenbitshifter_output), .in3(sixteenbitshifter_14_sixteenbitshifter_output),
    .in4(sixteenbitshifter_19_sixteenbitshifter_output), .in5(sixteenbitshifter_23_sixteenbitshifter_output),
    .in6(sixteenbitshifter_26_sixteenbitshifter_output), .in7(sixteenbitshifter_28_sixteenbitshifter_output),
    .out(leftshifter_output), .sel(leftshifter_muxselector));
endmodule

module comparison (
  input  [15:0] comparison_input_a,
  input  [15:0] comparison_input_b,
  output out_3
);

  wire xnor_1_out, xnor_2_out, xnor_3_out, xnor_4_out, xnor_5_out, xnor_6_out, xnor_7_out, xnor_8_out,
       xnor_9_out, xnor_10_out, xnor_11_out, xnor_12_out, xnor_13_out, xnor_14_out, xnor_15_out, xnor_16_out;

  xnor xnor_1 (xnor_1_out, comparison_input_a[0], comparison_input_b[0]);
  xnor xnor_2 (xnor_2_out, comparison_input_a[1], comparison_input_b[1]);
  xnor xnor_3 (xnor_3_out, comparison_input_a[2], comparison_input_b[2]);
  xnor xnor_4 (xnor_4_out, comparison_input_a[3], comparison_input_b[3]);
  xnor xnor_5 (xnor_5_out, comparison_input_a[4], comparison_input_b[4]);
  xnor xnor_6 (xnor_6_out, comparison_input_a[5], comparison_input_b[5]);
  xnor xnor_7 (xnor_7_out, comparison_input_a[6], comparison_input_b[6]);
  xnor xnor_8 (xnor_8_out, comparison_input_a[7], comparison_input_b[7]);
  xnor xnor_9 (xnor_9_out, comparison_input_a[8], comparison_input_b[8]);
  xnor xnor_10 (xnor_10_out, comparison_input_a[9], comparison_input_b[9]);
  xnor xnor_11 (xnor_11_out, comparison_input_a[10], comparison_input_b[10]);
  xnor xnor_12 (xnor_12_out, comparison_input_a[11], comparison_input_b[11]);
  xnor xnor_13 (xnor_13_out, comparison_input_a[12], comparison_input_b[12]);
  xnor xnor_14 (xnor_14_out, comparison_input_a[13], comparison_input_b[13]);
  xnor xnor_15 (xnor_15_out, comparison_input_a[14], comparison_input_b[14]);
  xnor xnor_16 (xnor_16_out, comparison_input_a[15], comparison_input_b[15]);
  and and_1 (out_3, xnor_1_out, xnor_2_out, xnor_3_out, xnor_4_out, xnor_5_out, xnor_6_out, xnor_7_out, xnor_8_out, xnor_9_out, xnor_10_out, xnor_11_out, xnor_12_out, xnor_13_out, xnor_14_out, xnor_15_out, xnor_16_out);
endmodule

module signextend (
  input  [5:0] signextend_immediate,
  output [15:0] signextend_output
);


  assign signextend_output = {{11{signextend_immediate[5]}}, signextend_immediate[4:0]};
endmodule

module instructions (
  input  [15:0] instructions_input,
  output [2:0] instructions_shamt,
  output [2:0] instructions_rd,
  output [2:0] instructions_rt,
  output [2:0] instructions_rs,
  output [3:0] instructions_opcode,
  output [5:0] instructions_immediate,
  output [11:0] instructions_address
);


  assign instructions_address = instructions_input[11:0];
  assign instructions_immediate = instructions_input[5:0];
  assign instructions_opcode = instructions_input[15:12];
  assign instructions_rd = instructions_input[5:3];
  assign instructions_rs = instructions_input[11:9];
  assign instructions_rt = instructions_input[8:6];
  assign instructions_shamt = instructions_input[2:0];
endmodule

module control (
  input  [3:0] control_optype,
  output control_output,
  output control_input,
  output control_lw,
  output control_sw,
  output control_beq,
  output control_bgt,
  output control_aluop,
  output control_j,
  output control_jal,
  output control_jr,
  output control_we,
  output control_immediate,
  output control_rdst
);

  wire decoder_1_out6, decoder_1_out7, decoder_1_out8, decoder_1_out9, decoder_1_out10, decoder_1_out11,
       decoder_1_out12, decoder_1_out13;

  Decoder #(.select(4)) decoder_1 (
    .out0(control_output), .out1(control_input), .out2(control_lw), .out3(control_sw), .out4(control_beq),
    .out5(control_bgt), .out6(decoder_1_out6), .out7(decoder_1_out7), .out8(decoder_1_out8),
    .out9(decoder_1_out9), .out10(decoder_1_out10), .out11(decoder_1_out11), .out12(decoder_1_out12),
    .out13(decoder_1_out13), .out14(control_jal), .out15(control_jr), .sel(control_optype), .en(1'b1));
  or or_1 (control_aluop, control_lw, control_sw, decoder_1_out6, decoder_1_out7, decoder_1_out8, decoder_1_out9, decoder_1_out10, decoder_1_out11, decoder_1_out12);
  or or_2 (control_j, decoder_1_out13, control_jal);
  or or_3 (control_we, control_input, control_lw, decoder_1_out6, decoder_1_out7, decoder_1_out8, decoder_1_out10, decoder_1_out11, decoder_1_out12, decoder_1_out9, control_jal);
  or or_4 (control_immediate, control_lw, control_sw, decoder_1_out8, decoder_1_out11, decoder_1_out12);
  or or_5 (control_rdst, control_input, control_beq, control_jal, control_bgt, decoder_1_out6, control_sw, decoder_1_out7, decoder_1_out12, decoder_1_out9, decoder_1_out10, decoder_1_out11);
endmodule

module pc (
  input  [15:0] pc_address_input,
  input  pc_clk,
  input  reset,
  output [15:0] pc_address_output
);

  register register_1 (
    .reg_datain(pc_address_input), .reg_clk(pc_clk), .reg_we(1'b1), .reset(reset),
    .reg_dataout(pc_address_output));
endmodule

module alujump (
  input  [11:0] alujump_j,
  input  [15:0] alujump_pc,
  output [15:0] alujump_jaddress
);


  assign alujump_jaddress = {alujump_pc[15:12], alujump_j};
endmodule

module alubranch (
  input  [15:0] alubranch_pc,
  input  [15:0] alubranch_immediate,
  output [15:0] alubranch_address
);

  sixteenbitadder sixteenbitadder_1 (
    .sixteenbitadder_b(alubranch_immediate), .sixteenbitadder_a(alubranch_pc),
    .sixteenbitadder_sum(alubranch_address), .sixteenbitadder_op(1'b0));  // open: sixteenbitadder_ovf
endmodule

module alupcincrement (
  input  [15:0] alupcincrement_input,
  output [15:0] out_2
);

  sixteenbitadder sixteenbitadder_1 (
    .sixteenbitadder_b(16'h1), .sixteenbitadder_a(alupcincrement_input), .sixteenbitadder_sum(out_2),
    .sixteenbitadder_op(1'b0));  // open: sixteenbitadder_ovf
endmodule

module aludecode (
  input  aludecode_controlop,
  input  [3:0] aludecode_opcode,
  output [2:0] aludecode_optype
);

  wire add_out, addi_out, and_2_out, and_3_out, and_4_out, and_5_out, and_6_out, and_7_out, and_8_out,
       and_out, leftshift_out, lw_out, not_1_out, not_2_out, not_3_out, not_4_out, not_5_out, not_6_out,
       not_7_out, not_8_out, not_9_out, not_10_out, not_11_out, not_12_out, not_13_out, not_14_out,
       not_15_out, not_16_out, not_17_out, not_18_out, or_2_out, or_3_out, or_out, rightshift_out, sub_out,
       sw_out;

  not not_1 (not_1_out, aludecode_opcode[0]);
  not not_2 (not_2_out, aludecode_opcode[3]);
  not not_3 (not_3_out, aludecode_opcode[3]);
  not not_4 (not_4_out, aludecode_opcode[1]);
  not not_5 (not_5_out, aludecode_opcode[2]);
  not not_6 (not_6_out, aludecode_opcode[0]);
  not not_7 (not_7_out, aludecode_opcode[1]);
  not not_8 (not_8_out, aludecode_opcode[2]);
  not not_9 (not_9_out, aludecode_opcode[0]);
  not not_10 (not_10_out, aludecode_opcode[2]);
  not not_11 (not_11_out, aludecode_opcode[0]);
  not not_12 (not_12_out, aludecode_opcode[1]);
  not not_13 (not_13_out, aludecode_opcode[2]);
  not not_14 (not_14_out, aludecode_opcode[0]);
  not not_15 (not_15_out, aludecode_opcode[2]);
  not not_16 (not_16_out, aludecode_opcode[3]);
  not not_17 (not_17_out, aludecode_opcode[2]);
  not not_18 (not_18_out, aludecode_opcode[3]);
  and \or  (or_out, not_1_out, aludecode_opcode[1], aludecode_opcode[2], not_2_out);
  and \and  (and_out, aludecode_opcode[0], aludecode_opcode[1], aludecode_opcode[2], not_3_out);
  and add (add_out, aludecode_opcode[0], not_4_out, not_5_out, aludecode_opcode[3]);
  and addi (addi_out, not_6_out, not_7_out, not_8_out, aludecode_opcode[3]);
  and sub (sub_out, not_9_out, aludecode_opcode[1], not_10_out, aludecode_opcode[3]);
  and leftshift (leftshift_out, not_11_out, not_12_out, aludecode_opcode[2], aludecode_opcode[3]);
  and rightshift (rightshift_out, aludecode_opcode[0], aludecode_opcode[1], not_13_out, aludecode_opcode[3]);
  and lw (lw_out, not_14_out, aludecode_opcode[1], not_15_out, not_16_out);
  and sw (sw_out, aludecode_opcode[0], aludecode_opcode[1], not_17_out, not_18_out);
  or or_2 (or_2_out, add_out, addi_out);
  or or_3 (or_3_out, lw_out, sw_out);
  and and_2 (and_2_out, or_out, aludecode_controlop);
  assign aludecode_optype = and_2_out ? 3'b000 : 3'bz;  // Controlled_Buffer controlled_buffer_1
  and and_3 (and_3_out, and_out, aludecode_controlop);
  assign aludecode_optype = and_3_out ? 3'b001 : 3'bz;  // Controlled_Buffer controlled_buffer_2
  and and_4 (and_4_out, or_2_out, aludecode_controlop);
  assign aludecode_optype = and_4_out ? 3'b010 : 3'bz;  // Controlled_Buffer controlled_buffer_3
  and and_5 (and_5_out, sub_out, aludecode_controlop);
  assign aludecode_optype = and_5_out ? 3'b011 : 3'bz;  // Controlled_Buffer controlled_buffer_4
  and and_6 (and_6_out, leftshift_out, aludecode_controlop);
  assign aludecode_optype = and_7_out ? 3'b100 : 3'bz;  // Controlled_Buffer controlled_buffer_5
  and and_7 (and_7_out, rightshift_out, aludecode_controlop);
  assign aludecode_optype = and_6_out ? 3'b101 : 3'bz;  // Controlled_Buffer controlled_buffer_6
  and and_8 (and_8_out, or_3_out, aludecode_controlop);
  assign aludecode_optype = and_8_out ? 3'b110 : 3'bz;  // Controlled_Buffer controlled_buffer_7
endmodule

module memorylatch (
  input  [15:0] address,
  input  WE,
  input  clk,
  input  [15:0] data_in,
  output [15:0] address_latched,
  output WE_latched,
  output OE_latched,
  output [15:0] data_in_latched
);

  wire d_ff_1_q;
  wire [15:0] register_1_q;

  Register #(.width(16), .trigger("falling")) register_1 (
    .D(address), .en(WE), .clk(clk), .Q(register_1_q));  // open: clr
  D_Flip_Flop #(.trigger("falling")) d_ff_1 (.D(WE), .clk(clk), .Q(d_ff_1_q));  // open: Qn, preset, reset
  Register #(.width(16), .trigger("falling")) register_2 (
    .D(data_in), .en(WE), .clk(clk), .Q(data_in_latched));  // open: clr
  Multiplexer #(.width(16), .enable("false")) multiplexer_1 (
    .in0(address), .in1(register_1_q), .out(address_latched), .sel(d_ff_1_q));
  and and_1 (WE_latched, clk, d_ff_1_q);
  not not_1 (OE_latched, WE_latched);
endmodule
