// Logisim project fsm.circ as structural Verilog: 1 circuit, main circuit main
module main (
  input  in1,
  input  in2,
  output out
);

  wire and_1_out, and_2_out, and_3_out, and_4_out, and_5_out, and_6_out, and_7_out, clock_1_out, D0_q, D0_qn,
       D1_q, D1_qn, D2_q, D2_qn, not_1_out, not_2_out, not_3_out, or_1_out, or_2_out, or_3_out, xor_1_out,
       xor_2_out, xor_3_out, xor_4_out, xor_5_out, xor_6_out, xor_7_out;

  xor xor_1 (xor_1_out, in1, in2);
  xor xor_2 (xor_2_out, in1, in2);
  xor xor_3 (xor_3_out, in1, in2);
  xor xor_4 (xor_4_out, in1, in2);
  xor xor_5 (xor_5_out, in1, in2);
  xor xor_6 (xor_6_out, in1, in2);
  xor xor_7 (xor_7_out, D1_q, D0_q);
  not not_1 (not_1_out, xor_4_out);
  not not_2 (not_2_out, xor_5_out);
  not not_3 (not_3_out, xor_6_out);
  and and_1 (and_1_out, xor_1_out, D0_q, D1_q, D2_qn);
  and and_2 (and_2_out, xor_1_out, D0_qn, D1_qn);
  and and_3 (and_3_out, D0_q, D1_qn, D2_qn, xor_2_out);
  and and_4 (and_4_out, D0_qn, D1_q, D2_qn, xor_3_out);
  and and_5 (and_5_out, D0_q, D1_q, D2_qn, not_1_out);
  and and_6 (and_6_out, D0_qn, D1_qn, D2_q, not_2_out);
  and and_7 (and_7_out, D0_qn, D1_qn, D2_qn, not_3_out);
  Clock clock_1 (.out(clock_1_out));
  D_Flip_Flop D2 (.D(or_1_out), .clk(clock_1_out), .Q(D2_q), .Qn(D2_qn));  // open: preset, reset
  or or_1 (or_1_out, and_1_out, and_2_out);
  D_Flip_Flop D1 (.D(or_2_out), .clk(clock_1_out), .Q(D1_q), .Qn(D1_qn));  // open: preset, reset
  or or_2 (or_2_out, and_3_out, and_4_out, and_5_out, and_6_out);
  D_Flip_Flop D0 (.D(or_3_out), .clk(clock_1_out), .Q(D0_q), .Qn(D0_qn));  // open: preset, reset
  or or_3 (or_3_out, and_7_out, xor_7_out);
  and and_8 (out, D2_qn, D1_q);
endmodule
